// Logisim project CPU_2.0.circ as structural Verilog: 5 circuits, main circuit main
module main (
  input  SUB,
  input  [2:0] SELECT,
  input  [3:0] A,
  input  [3:0] B,
  output X4,
  output X3,
  output X2,
  output X1,
  output X0
);

  wire basic_alu_1_cout, basic_alu_2_cout, basic_alu_3_cout, basic_alu_4_cout, xor_1_out;

  Basic_ALU basic_alu_1 (
    .A(A[0]), .B(B[0]), .RESULT(X0), .Cout(basic_alu_1_cout), .Cin(SUB), .SUB(SUB), .SELECT_LINE(SELECT));
  Basic_ALU basic_alu_2 (
    .A(A[1]), .B(B[1]), .RESULT(X1), .Cout(basic_alu_2_cout), .Cin(basic_alu_1_cout), .SUB(SUB),
    .SELECT_LINE(SELECT));
  Basic_ALU basic_alu_3 (
    .A(A[2]), .B(B[2]), .RESULT(X2), .Cout(basic_alu_3_cout), .Cin(basic_alu_2_cout), .SUB(SUB),
    .SELECT_LINE(SELECT));
  Basic_ALU basic_alu_4 (
    .A(A[3]), .B(B[3]), .RESULT(X3), .Cout(basic_alu_4_cout), .Cin(basic_alu_3_cout), .SUB(SUB),
    .SELECT_LINE(SELECT));
  xor xor_1 (xor_1_out, SUB, basic_alu_4_cout);
  Multiplexer #(.select(3)) multiplexer_1 (
    .in0(1'b0), .in1(1'b0), .in2(1'b0), .in3(1'b0), .in4(1'b0), .in5(1'b0), .in6(xor_1_out), .in7(1'b0),
    .out(X4), .sel(SELECT));  // open: en
  Hex_Digit_Display hex_digit_display_1 (.value({3'b000, X4}));  // open: dp
  Hex_Digit_Display hex_digit_display_2 (.value({X3, X2, X1, X0}));  // open: dp

  // Notes on the sheet:
  //   000 for OR logic
  //   001 for AND logic
  //   010 for EXOR logic
  //   011 for NOR logic
  //   100 for NAND logic
  //   101 for EXNOR logic
  //   110 for add/sub
  //   111 wiil be indetermined
endmodule

module Basic_ALU (
  input  SUB,
  input  A,
  input  B,
  input  Cin,
  input  [2:0] SELECT_LINE,
  output RESULT,
  output Cout
);

  wire adder_1_out, and_1_out, nand_1_out, nor_1_out, or_1_out, xnor_1_out, xor_1_out, xor_2_out;

  xor xor_1 (xor_1_out, B, SUB);
  or or_1 (or_1_out, A, B);
  and and_1 (and_1_out, A, B);
  xor xor_2 (xor_2_out, A, B);
  nor nor_1 (nor_1_out, A, B);
  nand nand_1 (nand_1_out, A, B);
  xnor xnor_1 (xnor_1_out, A, B);
  Adder #(.width(1)) adder_1 (.a(A), .b(xor_1_out), .out(adder_1_out), .cin(Cin), .cout(Cout));
  Multiplexer #(.select(3)) multiplexer_1 (
    .in0(or_1_out), .in1(and_1_out), .in2(xor_2_out), .in3(nor_1_out), .in4(nand_1_out), .in5(xnor_1_out),
    .in6(adder_1_out), .out(RESULT), .sel(SELECT_LINE));  // open: in7, en

  // Notes on the sheet:
  //   000 for OR logic
  //   001 for AND logic
  //   010 for EXOR logic
  //   011 for NOR logic
  //   100 for NAND logic
  //   110 for EXNOR logic
  //   111 wiil be indetermined
endmodule

module Binary_Cell_Memeory (
  input  SELECT,
  input  INPUT,
  input  READ_WRITE_prime,
  output OUTPUT
);

  wire and_1_out, d_ff_1_q, not_1_out;

  and and_1 (and_1_out, SELECT, not_1_out);
  not not_1 (not_1_out, READ_WRITE_prime);
  D_Flip_Flop d_ff_1 (.clk(and_1_out), .D(INPUT), .Q(d_ff_1_q));  // open: Qn, preset, en, reset
  and and_2 (OUTPUT, SELECT, d_ff_1_q, READ_WRITE_prime);
endmodule

module _5_7_Memory (
  input  A4,
  input  A3,
  input  A2,
  input  A1,
  input  A0,
  input  in_6,
  input  [2:0] in_7,
  input  READ_WRITE_prime,
  output A4_2,
  output A3_2,
  output A2_2,
  output A1_2,
  output A0_2
);

  wire binary_cell_memeory_1_output, binary_cell_memeory_2_output, binary_cell_memeory_3_output,
       binary_cell_memeory_4_output, binary_cell_memeory_5_output, binary_cell_memeory_6_output,
       binary_cell_memeory_7_output, binary_cell_memeory_8_output, binary_cell_memeory_9_output,
       binary_cell_memeory_10_output, binary_cell_memeory_11_output, binary_cell_memeory_12_output,
       binary_cell_memeory_13_output, binary_cell_memeory_14_output, binary_cell_memeory_15_output,
       binary_cell_memeory_16_output, binary_cell_memeory_17_output, binary_cell_memeory_18_output,
       binary_cell_memeory_19_output, binary_cell_memeory_20_output, binary_cell_memeory_21_output,
       binary_cell_memeory_22_output, binary_cell_memeory_23_output, binary_cell_memeory_24_output,
       binary_cell_memeory_25_output, binary_cell_memeory_26_output, binary_cell_memeory_27_output,
       binary_cell_memeory_28_output, binary_cell_memeory_29_output, binary_cell_memeory_30_output,
       binary_cell_memeory_31_output, binary_cell_memeory_32_output, binary_cell_memeory_33_output,
       binary_cell_memeory_34_output, binary_cell_memeory_35_output, demultiplexer_1_out0,
       demultiplexer_1_out1, demultiplexer_1_out2, demultiplexer_1_out3, demultiplexer_1_out4,
       demultiplexer_1_out5, demultiplexer_1_out6;

  Demultiplexer #(.select(3)) demultiplexer_1 (
    .out0(demultiplexer_1_out0), .out1(demultiplexer_1_out1), .out2(demultiplexer_1_out2),
    .out3(demultiplexer_1_out3), .out4(demultiplexer_1_out4), .out5(demultiplexer_1_out5),
    .out6(demultiplexer_1_out6), .in(1'b1), .sel(in_7), .en(in_6));  // open: out7
  Binary_Cell_Memeory binary_cell_memeory_1 (
    .INPUT(A4), .OUTPUT(binary_cell_memeory_1_output), .SELECT(demultiplexer_1_out0),
    .READ_WRITE_prime(READ_WRITE_prime));
  Binary_Cell_Memeory binary_cell_memeory_2 (
    .INPUT(A4), .OUTPUT(binary_cell_memeory_2_output), .SELECT(demultiplexer_1_out1),
    .READ_WRITE_prime(READ_WRITE_prime));
  Binary_Cell_Memeory binary_cell_memeory_3 (
    .INPUT(A4), .OUTPUT(binary_cell_memeory_3_output), .SELECT(demultiplexer_1_out2),
    .READ_WRITE_prime(READ_WRITE_prime));
  Binary_Cell_Memeory binary_cell_memeory_4 (
    .INPUT(A4), .OUTPUT(binary_cell_memeory_4_output), .SELECT(demultiplexer_1_out3),
    .READ_WRITE_prime(READ_WRITE_prime));
  Binary_Cell_Memeory binary_cell_memeory_5 (
    .INPUT(A4), .OUTPUT(binary_cell_memeory_5_output), .SELECT(demultiplexer_1_out4),
    .READ_WRITE_prime(READ_WRITE_prime));
  Binary_Cell_Memeory binary_cell_memeory_6 (
    .INPUT(A4), .OUTPUT(binary_cell_memeory_6_output), .SELECT(demultiplexer_1_out5),
    .READ_WRITE_prime(READ_WRITE_prime));
  Binary_Cell_Memeory binary_cell_memeory_7 (
    .INPUT(A4), .OUTPUT(binary_cell_memeory_7_output), .SELECT(demultiplexer_1_out6),
    .READ_WRITE_prime(READ_WRITE_prime));
  or or_1 (A4_2, binary_cell_memeory_7_output, binary_cell_memeory_6_output, binary_cell_memeory_5_output, binary_cell_memeory_4_output, binary_cell_memeory_3_output, binary_cell_memeory_2_output, binary_cell_memeory_1_output);
  Binary_Cell_Memeory binary_cell_memeory_8 (
    .INPUT(A3), .OUTPUT(binary_cell_memeory_8_output), .SELECT(demultiplexer_1_out0),
    .READ_WRITE_prime(READ_WRITE_prime));
  Binary_Cell_Memeory binary_cell_memeory_9 (
    .INPUT(A3), .OUTPUT(binary_cell_memeory_9_output), .SELECT(demultiplexer_1_out1),
    .READ_WRITE_prime(READ_WRITE_prime));
  Binary_Cell_Memeory binary_cell_memeory_10 (
    .INPUT(A3), .OUTPUT(binary_cell_memeory_10_output), .SELECT(demultiplexer_1_out2),
    .READ_WRITE_prime(READ_WRITE_prime));
  Binary_Cell_Memeory binary_cell_memeory_11 (
    .INPUT(A3), .OUTPUT(binary_cell_memeory_11_output), .SELECT(demultiplexer_1_out3),
    .READ_WRITE_prime(READ_WRITE_prime));
  Binary_Cell_Memeory binary_cell_memeory_12 (
    .INPUT(A3), .OUTPUT(binary_cell_memeory_12_output), .SELECT(demultiplexer_1_out4),
    .READ_WRITE_prime(READ_WRITE_prime));
  Binary_Cell_Memeory binary_cell_memeory_13 (
    .INPUT(A3), .OUTPUT(binary_cell_memeory_13_output), .SELECT(demultiplexer_1_out5),
    .READ_WRITE_prime(READ_WRITE_prime));
  Binary_Cell_Memeory binary_cell_memeory_14 (
    .INPUT(A3), .OUTPUT(binary_cell_memeory_14_output), .SELECT(demultiplexer_1_out6),
    .READ_WRITE_prime(READ_WRITE_prime));
  or or_2 (A3_2, binary_cell_memeory_14_output, binary_cell_memeory_13_output, binary_cell_memeory_12_output, binary_cell_memeory_11_output, binary_cell_memeory_10_output, binary_cell_memeory_9_output, binary_cell_memeory_8_output);
  Binary_Cell_Memeory binary_cell_memeory_15 (
    .INPUT(A2), .OUTPUT(binary_cell_memeory_15_output), .SELECT(demultiplexer_1_out0),
    .READ_WRITE_prime(READ_WRITE_prime));
  Binary_Cell_Memeory binary_cell_memeory_16 (
    .INPUT(A2), .OUTPUT(binary_cell_memeory_16_output), .SELECT(demultiplexer_1_out1),
    .READ_WRITE_prime(READ_WRITE_prime));
  Binary_Cell_Memeory binary_cell_memeory_17 (
    .INPUT(A2), .OUTPUT(binary_cell_memeory_17_output), .SELECT(demultiplexer_1_out2),
    .READ_WRITE_prime(READ_WRITE_prime));
  Binary_Cell_Memeory binary_cell_memeory_18 (
    .INPUT(A2), .OUTPUT(binary_cell_memeory_18_output), .SELECT(demultiplexer_1_out3),
    .READ_WRITE_prime(READ_WRITE_prime));
  Binary_Cell_Memeory binary_cell_memeory_19 (
    .INPUT(A2), .OUTPUT(binary_cell_memeory_19_output), .SELECT(demultiplexer_1_out4),
    .READ_WRITE_prime(READ_WRITE_prime));
  Binary_Cell_Memeory binary_cell_memeory_20 (
    .INPUT(A2), .OUTPUT(binary_cell_memeory_20_output), .SELECT(demultiplexer_1_out5),
    .READ_WRITE_prime(READ_WRITE_prime));
  Binary_Cell_Memeory binary_cell_memeory_21 (
    .INPUT(A2), .OUTPUT(binary_cell_memeory_21_output), .SELECT(demultiplexer_1_out6),
    .READ_WRITE_prime(READ_WRITE_prime));
  or or_3 (A2_2, binary_cell_memeory_21_output, binary_cell_memeory_20_output, binary_cell_memeory_19_output, binary_cell_memeory_18_output, binary_cell_memeory_17_output, binary_cell_memeory_16_output, binary_cell_memeory_15_output);
  Binary_Cell_Memeory binary_cell_memeory_22 (
    .INPUT(A1), .OUTPUT(binary_cell_memeory_22_output), .SELECT(demultiplexer_1_out0),
    .READ_WRITE_prime(READ_WRITE_prime));
  Binary_Cell_Memeory binary_cell_memeory_23 (
    .INPUT(A1), .OUTPUT(binary_cell_memeory_23_output), .SELECT(demultiplexer_1_out1),
    .READ_WRITE_prime(READ_WRITE_prime));
  Binary_Cell_Memeory binary_cell_memeory_24 (
    .INPUT(A1), .OUTPUT(binary_cell_memeory_24_output), .SELECT(demultiplexer_1_out2),
    .READ_WRITE_prime(READ_WRITE_prime));
  Binary_Cell_Memeory binary_cell_memeory_25 (
    .INPUT(A1), .OUTPUT(binary_cell_memeory_25_output), .SELECT(demultiplexer_1_out3),
    .READ_WRITE_prime(READ_WRITE_prime));
  Binary_Cell_Memeory binary_cell_memeory_26 (
    .INPUT(A1), .OUTPUT(binary_cell_memeory_26_output), .SELECT(demultiplexer_1_out4),
    .READ_WRITE_prime(READ_WRITE_prime));
  Binary_Cell_Memeory binary_cell_memeory_27 (
    .INPUT(A1), .OUTPUT(binary_cell_memeory_27_output), .SELECT(demultiplexer_1_out5),
    .READ_WRITE_prime(READ_WRITE_prime));
  Binary_Cell_Memeory binary_cell_memeory_28 (
    .INPUT(A1), .OUTPUT(binary_cell_memeory_28_output), .SELECT(demultiplexer_1_out6),
    .READ_WRITE_prime(READ_WRITE_prime));
  or or_4 (A1_2, binary_cell_memeory_28_output, binary_cell_memeory_27_output, binary_cell_memeory_26_output, binary_cell_memeory_25_output, binary_cell_memeory_24_output, binary_cell_memeory_23_output, binary_cell_memeory_22_output);
  Binary_Cell_Memeory binary_cell_memeory_29 (
    .INPUT(A0), .OUTPUT(binary_cell_memeory_29_output), .SELECT(demultiplexer_1_out0),
    .READ_WRITE_prime(READ_WRITE_prime));
  Binary_Cell_Memeory binary_cell_memeory_30 (
    .INPUT(A0), .OUTPUT(binary_cell_memeory_30_output), .SELECT(demultiplexer_1_out1),
    .READ_WRITE_prime(READ_WRITE_prime));
  Binary_Cell_Memeory binary_cell_memeory_31 (
    .INPUT(A0), .OUTPUT(binary_cell_memeory_31_output), .SELECT(demultiplexer_1_out2),
    .READ_WRITE_prime(READ_WRITE_prime));
  Binary_Cell_Memeory binary_cell_memeory_32 (
    .INPUT(A0), .OUTPUT(binary_cell_memeory_32_output), .SELECT(demultiplexer_1_out3),
    .READ_WRITE_prime(READ_WRITE_prime));
  Binary_Cell_Memeory binary_cell_memeory_33 (
    .INPUT(A0), .OUTPUT(binary_cell_memeory_33_output), .SELECT(demultiplexer_1_out4),
    .READ_WRITE_prime(READ_WRITE_prime));
  Binary_Cell_Memeory binary_cell_memeory_34 (
    .INPUT(A0), .OUTPUT(binary_cell_memeory_34_output), .SELECT(demultiplexer_1_out5),
    .READ_WRITE_prime(READ_WRITE_prime));
  Binary_Cell_Memeory binary_cell_memeory_35 (
    .INPUT(A0), .OUTPUT(binary_cell_memeory_35_output), .SELECT(demultiplexer_1_out6),
    .READ_WRITE_prime(READ_WRITE_prime));
  or or_5 (A0_2, binary_cell_memeory_35_output, binary_cell_memeory_34_output, binary_cell_memeory_33_output, binary_cell_memeory_32_output, binary_cell_memeory_31_output, binary_cell_memeory_30_output, binary_cell_memeory_29_output);
  Hex_Digit_Display hex_digit_display_1 (.value({A3, A2, A1, A0}));  // open: dp
  Hex_Digit_Display hex_digit_display_2 (.value({3'b000, A4}));  // open: dp
  Hex_Digit_Display hex_digit_display_3 (.value({3'b000, A4_2}));  // open: dp
  Hex_Digit_Display hex_digit_display_4 (.value({A3_2, A2_2, A1_2, A0_2}));  // open: dp

  // Notes on the sheet:
  //   7X5 MEMORY UNIT
endmodule

module CPU2_0 (
  input  [3:0] A,
  input  [3:0] B,
  input  SUB,
  input  [2:0] in_4,
  input  ENABLE,
  input  READ_1,
  output out_7,
  output out_8,
  output out_9,
  output out_10,
  output out_11
);

  wire main_1_x0, main_1_x1, main_1_x2, main_1_x3, main_1_x4;

  main main_1 (
    .A(A), .B(B), .SUB(SUB), .SELECT(in_4), .X4(main_1_x4), .X3(main_1_x3), .X2(main_1_x2), .X1(main_1_x1),
    .X0(main_1_x0));
  _5_7_Memory u_5_7_memory_1 (
    .in_6(ENABLE), .in_7(in_4), .READ_WRITE_prime(READ_1), .A4_2(out_7), .A3_2(out_8), .A2_2(out_9),
    .A1_2(out_10), .A0_2(out_11), .A4(main_1_x4), .A3(main_1_x3), .A2(main_1_x2), .A1(main_1_x1),
    .A0(main_1_x0));
  Hex_Digit_Display hex_digit_display_1 (.value({3'b000, out_7}));  // open: dp
  Hex_Digit_Display hex_digit_display_2 (.value({out_8, out_9, out_10, out_11}));  // open: dp

  // Notes on the sheet:
  //   WRITE(0)
endmodule
